# Fritzing sketch B2EMO (saved by Fritzing 0.9.3b)

parts:
  Part1 = Arduino Nano (Rev3.0)
  Part2 = NRF24L01+ Breakout Board
  J1 = Camdenboss CTB0158-2 [part_number=CTB0158-2 package=THT]
  S1 = Toggle Switch [package=THT]
  LED1 = LED - 5mm [color="Red (633nm)" package="5 mm [THT]"]
  LED2 = LEDs [package=led10mm]
  BAT1 = Battery Holders [package=lipo-1100mAh]
  L298N1 = L298N DC motor driver
  L298N2 = L298N DC motor driver
  C1 = Capacitor Polarized [package=cpol-radial-100uf-25v]
  M1 = DC Motor
  M2 = DC Motor
  M3 = DC Motor
  M4 = DC Motor
  R3 = Resistor [tolerance=±5% resistance=220 package="0402 [SMD]"]
  R4 = Resistor [tolerance=±5% resistance=220 package="0402 [SMD]"]
  J3 = Camdenboss CTB0158-2 [part_number=CTB0158-2 package=THT]
  J4 = Camdenboss CTB0158-2 [part_number=CTB0158-2 package=THT]
  M5 = DC Motor
  J5 = Camdenboss CTB0158-2 [part_number=CTB0158-2 package=THT]
  BAT2 = BC9VPC [package=bc9vpc]
  S2 = Toggle Switch [package=THT]
  J6 = Camdenboss CTB0158-2 [part_number=CTB0158-2 package=THT]

nets:
  N1: Part1.D2, L298N1.ENB
  N2: Part1.D3, L298N1.IN4
  N3: Part1.D4, L298N1.IN3
  N4: Part1.D5, L298N1.IN2
  N5: Part1.D6, L298N1.IN1
  N6: Part1.D7, L298N1.ENA
  N7: Part1.D8, Part2.CE
  N8: Part1.D9, L298N2.ENB
  N9: Part1.D10, Part2.CS
  N10: Part1.D11/MOSI, Part2.MOSI
  N11: Part1.D12/MISO, Part2.MISO
  N12: Part1.VIN, S2.L2
  GND: Part1.GND, Part2.GND, C1.-, J3.pin2, J5.terminal_1, J6.pin1
  N13: Part1.A5, J6.pin2
  N14: Part1.A4, J4.pin2
  N15: Part1.A3, J3.pin1
  N16: Part1.A2, J4.pin1
  N17: Part1.A1, L298N2.IN3
  N18: Part1.A0, L298N2.IN4
  3V3: Part1.3V3, Part2.VCC, C1.+
  N19: Part1.D13/SCK, Part2.SCK
  N20: J1.pin1, S1.L2
  GND_2: J1.pin2, L298N1.GND, L298N2.GND
  N21: J1.terminal_1, BAT1.+
  N22: J1.terminal_2, BAT1.-
  N23: S1.L1, L298N1.12V
  N24: LED1.cathode, LED2.C, J3.terminal_2
  N25: LED2.A, R3.Pin_1
  N26: L298N1.OUT1, M1.pin_2, M2.pin_2
  N27: L298N1.OUT2, M1.pin_1, M2.pin_1
  N28: L298N1.OUT3, M3.pin_1, M4.pin_1
  N29: L298N1.OUT4, M3.pin_2, M4.pin_2
  N30: L298N2.OUT3, M5.pin_2
  N31: L298N2.OUT4, M5.pin_1
  N32: R3.Pin_0, R4.Pin_0, J3.terminal_1
  N33: J5.pin1, BAT2.V+
  N34: J5.pin2, BAT2.V-
  N35: J5.terminal_2, S2.L1

notes:
  Left Motors
  Right Motors
  Gear Motor for threaded shaft
  Leds for eyes
  Free pins
  220 ohm resistor
  120 ohm resistor
  11.1 V Lipo battery for drivers
  100 mF capacitor
  B2EMO Reciever
  L298N Motor Driver
  9V battery for Arduino
  Slide switch

custom parts:
  L298N DC motor driver: 2x DC motor driver with 78M05 positive voltage regulator (7..35 V) L298N: max 46 V, 2 A Set 5 V Enable jumper to enable 5 V regultor (needed for the L298N) and +5 V output at screw terminal or supply external +5 V at screw terminal Set ENA and/or ENB to +5 V to enable motor permanently or supply ENA and/or ENB with PWM signal IN1 and IN2 set rotation directory for motor A (OUT1/OUT2) IN2 and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
